# Fritzing sketch nodemcu-rc522-led (saved by Fritzing 0.9.3b)
breadboards: 1

parts:
  U1 = NodeMCU V1.0
  Part1 = RFID-RC522-v2
  LED1 = RGB LED (com. cathode, rgb) [package="5 mm [THT]"]
  R1 = Resistor [tolerance=±5% resistance=1k package=THT]
  R2 = Resistor [tolerance=±5% resistance=1k package=THT]
  R3 = Resistor [tolerance=±5% resistance=1k package=THT]

nets:
  N1: U1.D1, Part1.RST
  N2: U1.D2, Part1.SDA
  N3: U1.D3, R3.Pin_0
  N4: U1.D4, R2.Pin_1
  3V3: U1.3V3, Part1.3.3V
  GND: U1.GND, Part1.GND, LED1.common_cathode
  N5: U1.D5, Part1.SCK
  N6: U1.D6, Part1.MISO
  N7: U1.D7, Part1.MOSI
  N8: U1.D8, R1.Pin_1
  N9: LED1.red_anode, R3.Pin_1
  N10: LED1.green_anode, R1.Pin_0, R2.Pin_0

custom parts:
  NodeMCU V1.0: ESP8266 based NodeMCU
  RFID-RC522-v2: A simple China made RFID-RC522 Reader; do check the pin labels, as this is a MFRC522 based clone.
